# Fritzing sketch raspberrypi_sensors (saved by Fritzing 0.9.2b)
breadboards: 1

parts:
  J1 = Cobbler Plus Cable
  IC1 = MCP3008 8-channel 10-bit ADC [part_number=MCP3008]
  R1 = Photocell (LDR) [package=THT]
  D1 = SOLAR-IXYS [package=solarbit-12x1]
  D2 = Diode [package=diode-hv]
  LED1 = LED - 5mm [color="Yellow (595nm)" package="5 mm [THT]"]
  LED2 = LED - 5mm [color="Red (633nm)" package="5 mm [THT]"]
  LED3 = LED - 5mm [color="Green (555nm)" package="5 mm [THT]"]
  T1 = TMP36 Temperature Sensor [package="TO92 [THT]"]
  R2 = Resistor [tolerance=±5% resistance=220 package="1206 [SMD]"]
  R3 = Resistor [tolerance=±5% resistance=10k package="1206 [SMD]"]
  R4 = Resistor [tolerance=±5% resistance=220 package="2512 [SMD]"]
  R5 = Resistor [tolerance=±5% resistance=220 package="2512 [SMD]"]
  R6 = Resistor [tolerance=±5% resistance=100k package=THT]
  R7 = Resistor [tolerance=±5% resistance=150k package="2512 [SMD]"]

nets:
  N1: J1.3V3, IC1.no_name_yet#15, IC1.no_name_yet#16, R1.pin_1, LED2.anode, T1.+Vs
  N2: J1.GND#5, IC1.no_name_yet#9, IC1.no_name_yet#14, D1.C, LED3.cathode, T1.GND, R3.Pin_0, R4.Pin_0, R5.Pin_1, R7.Pin_0
  N3: J1.#18, LED1.cathode
  N4: J1.MOSI, IC1.no_name_yet#11
  N5: J1.MISO, IC1.no_name_yet#12
  N6: J1.SCLK, IC1.no_name_yet#13
  N7: J1.CE0, IC1.no_name_yet#10
  N8: IC1.no_name_yet#1, R1.pin_0, R3.Pin_1
  N9: IC1.no_name_yet#2, T1.Vout
  N10: IC1.no_name_yet#3, R6.Pin_0, R7.Pin_1
  N11: D1.A, D2.A
  N12: D2.C, R2.Pin_0, R6.Pin_1
  N13: LED1.anode, R5.Pin_0
  N14: LED2.cathode, R4.Pin_1
  N15: LED3.anode, R2.Pin_1

custom parts:
  Cobbler Plus Cable: The Cobbler Plus is an add on prototyping board from Adafruit specifically designed for the Raspberry Pi B+ that can break out all those tasty power, GPIO, I2C and SPI pins from the 40-pin header onto a solderless breadboard. This set will make "cobbling together" prototypes with the Pi super easy. The Cobbler Plus can plug into any solderless breadboard.
